# Fritzing sketch ObstacleCar_1_Bridge_4wd (saved by Fritzing 0.9.4)
breadboards: 1

parts:
  Part1 = Arduino Uno (Rev3)
  S2 = H-Bridge with L298N
  HC-SR04_Sensor_1 = HC-SR04 Ultrasonic Distance Sensor
  M5 = DC Motor
  M6 = DC Motor
  M7 = DC Motor
  M8 = DC Motor
  VCC1 = Battery
  VCC2 = Battery  # not connected
  S3 = Toggle Switch [package=THT]
  VCC3 = Battery

nets:
  N1: Part1.D11_PWM/MOSI, HC-SR04_Sensor_1.ECHO
  N2: Part1.D12/MISO, HC-SR04_Sensor_1.TRIG
  GND: Part1.GND, S2.GND, HC-SR04_Sensor_1.GND, VCC3.-
  N3: Part1.D1/TX, S2.IN2
  N4: Part1.D2, S2.IN1
  N5: Part1.D3_PWM, S2.ENA
  N6: Part1.D4, S2.IN3
  N7: Part1.D5_PWM, S2.ENB
  N8: Part1.D6_PWM, S2.IN4
  5V: Part1.5V, S2.5V, HC-SR04_Sensor_1.VCC
  N9: S2.12V, S3.L2
  N10: S2.M1-01, M7.pin_2, M8.pin_2
  N11: S2.M1-02, M7.pin_1, M8.pin_1
  N12: S2.M2-01, M5.pin_2, M6.pin_2
  N13: S2.M2-02, M5.pin_1, M6.pin_1
  N14: VCC1.+, S3.COM

notes:
  5V Out of the H-Bridge is powering Arduino

custom parts:
  H-Bridge with L298N: h-bridge
