# Fritzing sketch ObstacleCar_2_Bridges_4wd (saved by Fritzing 0.9.4)

parts:
  Part1 = Arduino Uno (Rev3)
  S2 = H-Bridge with L298N
  HC-SR04_Sensor_1 = HC-SR04 Ultrasonic Distance Sensor  # not connected
  M5 = DC Motor
  M6 = DC Motor
  M7 = DC Motor
  M8 = DC Motor
  S3 = H-Bridge with L298N
  BAT5 = BC9VPC [package=bc9vpc]

nets:
  N1: Part1.D8, S3.IN4
  N2: Part1.D9_PWM, S3.ENB
  N3: Part1.D10_PWM/SS, S3.IN3
  N4: Part1.D11_PWM/MOSI, S3.ENA
  N5: Part1.D12/MISO, S3.IN1
  N6: Part1.D13/SCK, S3.IN2
  GND: Part1.GND, S2.GND, S3.GND, BAT5.V-
  N7: Part1.D2, S2.IN4
  N8: Part1.D3_PWM, S2.ENB
  N9: Part1.D4, S2.IN3
  N10: Part1.D5_PWM, S2.IN2
  N11: Part1.D6_PWM, S2.ENA
  N12: Part1.D7, S2.IN1
  5V: Part1.5V, S2.5V
  12V: S2.12V, S3.12V, BAT5.V+
  N13: S2.M1-01, M5.pin_2
  N14: S2.M1-02, M5.pin_1
  N15: S2.M2-01, M6.pin_2
  N16: S2.M2-02, M6.pin_1
  N17: M7.pin_1, S3.M2-02
  N18: M7.pin_2, S3.M2-01
  N19: M8.pin_1, S3.M1-02
  N20: M8.pin_2, S3.M1-01

notes:
  TODO:
  5V Out of the H-Bridge is powering Arduino
  How to split?

custom parts:
  H-Bridge with L298N: h-bridge
